// Logisim project control-logic.circ as structural Verilog: 1 circuit, main circuit control_logic
module control_logic (
  input  [31:0] Instruction,
  input  BrEq,
  input  BrLt,
  output PCSel,
  output RegWEn,
  output [2:0] ImmSel,
  output BrUn,
  output ASel,
  output BSel,
  output [3:0] ALUSel,
  output MemWEn,
  output [1:0] WBSel
);

  wire and_1_out, and_4_out, and_5_out, and_6_out, and_7_out, and_8_out, comparator_1_eq, comparator_2_eq,
       comparator_3_eq, comparator_4_eq, comparator_5_eq, comparator_6_eq, comparator_7_eq, comparator_8_eq,
       comparator_9_eq, comparator_10_eq, comparator_15_eq, comparator_16_eq, comparator_17_eq,
       comparator_18_eq, comparator_19_eq, comparator_20_eq, comparator_21_eq, comparator_22_eq, I_type,
       is_mul, is_mulh, is_mulhu, is_sra, is_sub, not_1_out, not_2_out, or_2_out, or_5_out, R_type, S_type;
  wire [2:0] multiplexer_7_out, multiplexer_8_out, multiplexer_9_out;
  wire [3:0] multiplexer_1_out, multiplexer_2_out, multiplexer_3_out, multiplexer_4_out, multiplexer_5_out,
       RI_Sel;

  Comparator #(.width(3)) comparator_1 (.a(Instruction[14:12]), .b(3'b000), .eq(comparator_1_eq));  // open: gt, lt
  Comparator #(.width(3)) comparator_2 (.a(Instruction[14:12]), .b(3'b101), .eq(comparator_2_eq));  // open: gt, lt
  Comparator #(.width(3)) comparator_3 (.a(Instruction[14:12]), .b(3'b111), .eq(comparator_3_eq));  // open: gt, lt
  Comparator #(.width(3)) comparator_4 (.a(Instruction[14:12]), .b(3'b100), .eq(comparator_4_eq));  // open: gt, lt
  Comparator #(.width(3)) comparator_5 (.a(Instruction[14:12]), .b(3'b110), .eq(comparator_5_eq));  // open: gt, lt
  Comparator #(.width(3)) comparator_6 (.a(Instruction[14:12]), .b(3'b001), .eq(comparator_6_eq));  // open: gt, lt
  not not_1 (not_1_out, BrLt);
  Multiplexer #(.select(3), .width(4)) multiplexer_1 (
    .in0(4'b0000), .in1(4'b0001), .in2(4'b0010), .in4(4'b0100), .in5(4'b0101), .in6(4'b0110), .in7(4'b0111),
    .out(multiplexer_1_out), .sel(Instruction[14:12]));  // open: in3
  Comparator #(.width(3)) comparator_7 (.a(Instruction[14:12]), .b(3'b101), .eq(comparator_7_eq));  // open: gt, lt
  Comparator #(.width(7)) comparator_8 (.a(Instruction[31:25]), .b(7'b0100000), .eq(comparator_8_eq));  // open: gt, lt
  Comparator #(.width(3)) comparator_9 (.a(Instruction[14:12]), .b(3'b000), .eq(comparator_9_eq));  // open: gt, lt
  Comparator #(.width(7)) comparator_10 (
    .a(Instruction[31:25]), .b(7'b0100000), .eq(comparator_10_eq));  // open: gt, lt
  and and_1 (and_1_out, comparator_1_eq, ASel, BrEq);
  not not_2 (not_2_out, BrEq);
  Multiplexer #(.width(4)) multiplexer_2 (
    .in0(multiplexer_1_out), .in1(4'b1101), .out(multiplexer_2_out), .sel(is_sra));
  and and_2 (is_sra, comparator_7_eq, R_type, comparator_8_eq);
  and and_3 (is_sub, comparator_9_eq, R_type, comparator_10_eq);
  and and_4 (and_4_out, comparator_2_eq, ASel, not_1_out);
  and and_5 (and_5_out, not_1_out, ASel, comparator_3_eq);
  and and_6 (and_6_out, BrLt, ASel, comparator_4_eq);
  and and_7 (and_7_out, BrLt, ASel, comparator_5_eq);
  and and_8 (and_8_out, ASel, not_2_out, comparator_6_eq);
  Multiplexer #(.width(4)) multiplexer_3 (
    .in0(multiplexer_2_out), .in1(4'b1100), .out(multiplexer_3_out), .sel(is_sub));
  Multiplexer #(.width(4)) multiplexer_4 (
    .in0(multiplexer_3_out), .in1(4'b1000), .out(multiplexer_4_out), .sel(is_mul));
  Multiplexer #(.width(4)) multiplexer_5 (
    .in0(multiplexer_4_out), .in1(4'b1001), .out(multiplexer_5_out), .sel(is_mulh));
  or or_1 (PCSel, and_1_out, and_4_out, and_5_out, and_6_out, and_7_out, and_8_out);
  Comparator #(.width(7)) comparator_11 (.a(Instruction[6:0]), .b(7'b1100011), .eq(ASel));  // open: gt, lt
  Comparator #(.width(7)) comparator_12 (.a(Instruction[6:0]), .b(7'b0010011), .eq(I_type));  // open: gt, lt
  Comparator #(.width(7)) comparator_13 (.a(Instruction[6:0]), .b(7'b0110011), .eq(R_type));  // open: gt, lt
  Comparator #(.width(7)) comparator_14 (.a(Instruction[6:0]), .b(7'b0100011), .eq(S_type));  // open: gt, lt
  Multiplexer #(.width(4)) multiplexer_6 (.in0(multiplexer_5_out), .in1(4'b1011), .out(RI_Sel), .sel(is_mulhu));
  Multiplexer #(.width(3)) multiplexer_7 (.in0(3'b000), .in1(3'b001), .out(multiplexer_7_out), .sel(S_type));
  Comparator #(.width(3)) comparator_15 (.a(Instruction[14:12]), .b(3'b000), .eq(comparator_15_eq));  // open: gt, lt
  Comparator #(.width(7)) comparator_16 (
    .a(Instruction[31:25]), .b(7'b0000001), .eq(comparator_16_eq));  // open: gt, lt
  Multiplexer #(.width(3)) multiplexer_8 (.in0(multiplexer_7_out), .in1(3'b010), .out(multiplexer_8_out), .sel(ASel));
  and and_9 (is_mul, comparator_15_eq, R_type, comparator_16_eq);
  Multiplexer #(.width(3)) multiplexer_9 (.in0(multiplexer_8_out), .in1(3'b011), .out(multiplexer_9_out), .sel(1'b0));
  or or_2 (or_2_out, R_type, I_type);
  Multiplexer #(.width(4)) multiplexer_10 (.in0(4'b0000), .in1(RI_Sel), .out(ALUSel), .sel(or_2_out));
  Comparator #(.width(3)) comparator_17 (.a(Instruction[14:12]), .b(3'b001), .eq(comparator_17_eq));  // open: gt, lt
  Comparator #(.width(7)) comparator_18 (
    .a(Instruction[31:25]), .b(7'b0000001), .eq(comparator_18_eq));  // open: gt, lt
  or or_3 (BSel, I_type, ASel);
  Multiplexer #(.width(3)) multiplexer_11 (.in0(multiplexer_9_out), .in1(3'b100), .out(ImmSel), .sel(1'b0));
  Comparator #(.width(3)) comparator_19 (.a(Instruction[14:12]), .b(3'b111), .eq(comparator_19_eq));  // open: gt, lt
  Comparator #(.width(3)) comparator_20 (.a(Instruction[14:12]), .b(3'b110), .eq(comparator_20_eq));  // open: gt, lt
  and and_10 (is_mulh, comparator_17_eq, R_type, comparator_18_eq);
  or or_4 (RegWEn, I_type, R_type);
  or or_5 (or_5_out, comparator_19_eq, comparator_20_eq);
  Comparator #(.width(3)) comparator_21 (.a(Instruction[14:12]), .b(3'b011), .eq(comparator_21_eq));  // open: gt, lt
  Comparator #(.width(7)) comparator_22 (
    .a(Instruction[31:25]), .b(7'b0000001), .eq(comparator_22_eq));  // open: gt, lt
  and and_11 (BrUn, ASel, or_5_out);
  and and_12 (is_mulhu, comparator_21_eq, R_type, comparator_22_eq);

  assign WBSel = 2'b01;

  // Other names for the same wires on the sheet: B_type = ASel; opcode[6:0] = Instruction[6:0];
  //   rd[4:0] = Instruction[11:7]; funct3[2:0] = Instruction[14:12]; rs1[4:0] = Instruction[19:15];
  //   rs2[4:0] = Instruction[24:20]; funct7[6:0] = Instruction[31:25]

  // Notes on the sheet:
  //   Decode
  //   add
  //   sll
  //   slt
  //   xor
  //   srl
  //   or
  //   and
  //   INPUTS to your circuit
  //   DON'T CHANGE THE LOCATIONS OF THE INPUTS AND OUTPUTS!
  //   OUTPUT from your circuit
endmodule
